# Fritzing sketch Final fritzing (saved by Fritzing 0.7.12b)
breadboards: 1

parts:
  J1 = Infrared Proximity Sensor
  Arduino1 = Arduino
  J2 = Basic Servo
  J3 = Basic Servo
  J4 = Basic Servo
  VCC1 = Battery

nets:
  N1: J1.Vout, Arduino1.D7
  GND: J1.GND, Arduino1.GND, J2.gnd, J3.gnd, J4.gnd, VCC1.-
  VCC: J1.Vcc, Arduino1.+5V
  N2: Arduino1.D10, J3.pulse
  N3: Arduino1.D9, J2.pulse
  N4: Arduino1.D8, J4.pulse
  VCC_2: J2.vcc, J3.vcc, J4.vcc, VCC1.+
